# Fritzing sketch configuration (saved by Fritzing 0.8.7b)
breadboards: 2

parts:
  LCD1 = LCD screen [part_number=SX09393]
  C1 = Capacitor [package=cap-pth-small2]
  R1 = Rotary Potentiometer (Large) [maximum_resistance=100kΩ package=THT]
  Raspberry_Pi1 = Raspberry Pi B rev1
  IC1 = MCP3008 8-channel 10-bit ADC [part_number=MCP3008]  # not connected
  C2 = Capacitor [package=cap-pth-small2]
  U1 = 74HC595 [package="DIP16 [THT]"]  # not connected
  U2 = 74HC595 [package="DIP16 [THT]"]  # not connected

nets:
  N1: LCD1.E, Raspberry_Pi1.5V
  N2: LCD1.DB0, Raspberry_Pi1.GPIO_14
  N3: LCD1.DB1, C1.1, R1.leg2, Raspberry_Pi1.3V3
  N4: C1.2, R1.leg1, C2.1
  N5: R1.wiper, C2.2
